# Fritzing sketch rpi-weather (saved by Fritzing 0.9.3b)

parts:
  Raspberry_Pi1 = Raspberry Pi B+
  0x70 = 8x8 LED Matrix (yellow)
  0x71 = 8x8 LED Matrix (yellow)
  0x72 = 8x8 LED Matrix (yellow)
  0x73 = 8x8 LED Matrix (yellow)

nets:
  N1: Raspberry_Pi1.GPIO2, 0x70.D, 0x71.D, 0x72.D, 0x73.D
  N2: Raspberry_Pi1.GPIO3, 0x70.C, 0x71.C, 0x72.C, 0x73.C
  N3: Raspberry_Pi1.GND, 0x70.-, 0x71.-, 0x72.-, 0x73.-
  N4: Raspberry_Pi1.5V, 0x70.+, 0x71.+, 0x72.+, 0x73.+

custom parts:
  8x8 LED Matrix (yellow): 8x8 LED Matrix with I2C control (yellow)
